# Fritzing sketch MovmentLogger_Schema (saved by Fritzing 1.0.1rc)

parts:
  Bauteil1 = Arduino Mega 2560 (Rev3)
  PIR1 = PIR sensor
  Bauteil2 = Bluetooth HC-05 Macho

nets:
  GND: Bauteil1.GND, PIR1.GND, Bauteil2.GND
  3V3: Bauteil1.3V3, Bauteil2.VCC
  N1: Bauteil1.D0_RX0, Bauteil2.TXD
  N2: Bauteil1.D1_TX0, Bauteil2.RXD
  5V: Bauteil1.5V, PIR1.VDD
  N3: Bauteil1.D53, PIR1.SIG
